# Fritzing sketch FanControl (saved by Fritzing 0.9.10b)

parts:
  Arduino_Nano = Arduino Nano (Rev3.0)
  16x2_LCD_Display = LCD1602-I2C
  DS1 = DS18B20 1-Wire Temperature Sensor [part_number=DS18B20]
  R1 = Resistor [tolerance=±5% power=0.25 resistance=4.7k package=THT]
  Roto_Switch = KY-040 Rotary encoder [package=THT]
  F1 = Fan - 4 wire [part_number="Noctua NF-A9x14 PWM" package=THT]
  F2 = Fan - 4 wire [part_number="Noctua NF-A9x14 PWM" package=THT]
  Power_12_Volts = Power plug

nets:
  GND: Arduino_Nano.GND, 16x2_LCD_Display.GND, DS1.GND, Roto_Switch.GND, F1.GND, F2.GND, Power_12_Volts.GND
  N1: Arduino_Nano.D2, Roto_Switch.CLK
  N2: Arduino_Nano.D3, Roto_Switch.DT
  N3: Arduino_Nano.D4, Roto_Switch.SW
  N4: Arduino_Nano.D5, F2.PWM
  N5: Arduino_Nano.D6, F1.PWM
  N6: Arduino_Nano.D7, DS1.DQ, R1.Pin_0
  N7: Arduino_Nano.D8, F2.Tach
  N8: Arduino_Nano.D9, F1.Tach
  VIN: Arduino_Nano.VIN, F1.Power, F2.Power, Power_12_Volts.VCC
  VCC: Arduino_Nano.5V, 16x2_LCD_Display.VCC, DS1.VDD, R1.Pin_1, Roto_Switch.Vcc
  N9: Arduino_Nano.A5, 16x2_LCD_Display.SCL
  N10: Arduino_Nano.A4, 16x2_LCD_Display.SDA

custom parts:
  LCD1602-I2C: A standard character display, usually with 2x16 characters. Comes in many colors with LCM1602 IIC attached.
  KY-040 Rotary encoder: KY-040 Rotary Encoder with switch on breakout borad from AZ Delivery
  Fan - 4 wire: Fan, 4 wire with tach.
